// Logisim project offline_2.circ as structural Verilog: 9 circuits, main circuit main
module main (
  input  A_sign,
  input  B_sign,
  input  [9:0] A_exp,
  input  [9:0] B_exp,
  input  [20:0] A_frac,
  input  [20:0] B_frac,
  output [20:0] out_7,
  output [20:0] out_8
);

  wire comparator_1_lt, comparator_2_lt, control_1_out_2, control_1_out_3;
  wire [4:0] n16_to_5_1_out_2;
  wire [15:0] exponent_diff_1_diff, multiplexer_1_out, n2_s_complimemnt_1_out_2;
  wire [31:0] n21_to_32_1_out_2, shifter_1_out;

  Exponent_diff exponent_diff_1 (.A(A_exp), .B(B_exp), .diff(exponent_diff_1_diff));  // open: C_out
  Comparator #(.width(16)) comparator_1 (
    .a(exponent_diff_1_diff), .b({16{1'b0}}), .lt(comparator_1_lt));  // open: gt, eq
  _2_s_complimemnt u_2_s_complimemnt_1 (.in_1(exponent_diff_1_diff), .out_2(n2_s_complimemnt_1_out_2));
  Control control_1 (.in_1(exponent_diff_1_diff), .out_2(control_1_out_2), .out_3(control_1_out_3));
  Multiplexer #(.width(16), .enable("false")) multiplexer_1 (
    .in0(exponent_diff_1_diff), .in1(n2_s_complimemnt_1_out_2), .out(multiplexer_1_out), .sel(comparator_1_lt));
  Multiplexer #(.width(21), .enable("false")) multiplexer_2 (
    .in0(B_frac), .in1(A_frac), .out(out_7), .sel(control_1_out_2));
  Multiplexer #(.width(21), .enable("false")) multiplexer_3 (
    .in0(B_frac), .in1(A_frac), .out(out_8), .sel(control_1_out_3));
  Comparator #(.width(16)) comparator_2 (.a(16'h20), .b(multiplexer_1_out), .lt(comparator_2_lt));  // open: gt, eq
  _16_to_5 u_16_to_5_1 (.in_1(multiplexer_1_out), .out_2(n16_to_5_1_out_2));
  _21_to_32 u_21_to_32_1 (.A(out_7), .out_2(n21_to_32_1_out_2));
  Shifter #(.width(32), .shift("lr")) shifter_1 (
    .in(n21_to_32_1_out_2), .\dist (n16_to_5_1_out_2), .out(shifter_1_out));
  // Probe on shifter_1_out

  // Notes on the sheet:
  //   goes to shift
endmodule

module _16_bit_adder (
  input  C_in,
  input  [15:0] A,
  input  [15:0] B,
  output [15:0] out_4,
  output out_5
);

  Adder #(.width(16)) adder_1 (.a(A), .b(B), .out(out_4), .cin(C_in), .cout(out_5));
endmodule

module _32_bit_adder (
  input  C_in,
  input  [31:0] A,
  input  [31:0] B,
  output [31:0] out_4,
  output out_5
);

  Adder #(.width(32)) adder_1 (.a(A), .b(B), .out(out_4), .cin(C_in), .cout(out_5));
endmodule

// Exp_diff
module Exponent_diff (
  input  [9:0] A,
  input  [9:0] B,
  output [15:0] diff,
  output C_out
);

  wire [9:0] not_1_out;

  assign not_1_out = ~B;  // NOT_Gate not_1, 10 bits wide
  _16_bit_adder u_16_bit_adder_1 (
    .C_in(1'b1), .A({{6{1'b0}}, A}), .B({{6{1'b1}}, not_1_out}), .out_4(diff), .out_5(C_out));
endmodule

module Control (
  input  [15:0] in_1,
  output out_2,
  output out_3
);

  not not_1 (out_3, in_1[15]);

  assign out_2 = in_1[15];
endmodule

// 2's
module _2_s_complimemnt (
  input  [15:0] in_1,
  output [15:0] out_2
);

  wire subtractor_1_bout;

  Subtractor #(.width(16)) subtractor_1 (.a({16{1'b0}}), .b(in_1), .out(out_2), .bin(1'b0), .bout(subtractor_1_bout));
endmodule

module _21_to_32 (
  input  [20:0] A,
  output [31:0] out_2
);


  assign out_2 = {{11{1'b0}}, A};
endmodule

module _16_to_5 (
  input  [15:0] in_1,
  output [4:0] out_2
);


  assign out_2 = in_1[4:0];
endmodule

module trial (
  input  [9:0] in_1
);

  Comparator #(.width(10), .mode("unsigned")) comparator_1 (.a(in_1), .b({10{1'b0}}));  // open: gt, eq, lt
endmodule
